// Logisim project labdarbad.circ as structural Verilog
module ALU (
  input  [7:0] x,
  input  [7:0] y
);

  ADD add_1 ();  // open: x, y, Z, BAF
  Multiplexer #(.select(5), .width(32)) multiplexer_1 ();  // open: in0, in1, in2, in3, in4, in5, in6, in7, in8, in9, in10, in11, in12, in13, in14, in15, in16, in17, in18, in19, in20, in21, in22, in23, in24, in25, in26, in27, in28, in29, in30, in31, out, sel, en
endmodule

module ADD (
  input  [7:0] x,
  input  [7:0] y,
  output [7:0] Z,
  output BAF
);

  wire vld_1_bof, vld_2_bof;
  wire [7:0] adder_1_out;
  wire [8:8] adder_1_cout, divider_1_rem;

  Adder adder_1 (.a(x), .b(y), .out(adder_1_out), .cin(1'b0), .cout(adder_1_cout[8]));
  VLD vld_1 (.in_1(x), .BOF(vld_1_bof));  // open: Z
  VLD vld_2 (.in_1(y), .BOF(vld_2_bof));  // open: Z
  Divider #(.width(9)) divider_1 (
    .a({adder_1_cout[8], adder_1_out}), .b(9'h97), .upper({9{1'b0}}), .rem({divider_1_rem[8], Z}));  // open: out
  or or_1 (BAF, vld_1_bof, vld_2_bof);
endmodule

module VLD (
  input  [7:0] in_1,
  output Z,
  output BOF
);

  Comparator #(.mode("unsigned")) comparator_1 (.a(in_1), .b(8'h97), .lt(Z));  // open: gt, eq
  not not_1 (BOF, Z);
endmodule

module NEG (
  input  a,
  input  b,
  input  c,
  input  d,
  input  e,
  input  f,
  input  g,
  input  h,
  output BAF,
  output Z1,
  output Z2,
  output Z3,
  output Z4,
  output Z5,
  output Z6,
  output Z7,
  output Z8
);

  wire and_1_out, and_2_out, not_1_out, not_2_out;

  or or_1 (Z1, h, g, f);
  or or_2 (Z4, h, g, f);
  or or_3 (Z6, h, g);
  not not_1 (not_1_out, g);
  and and_1 (and_1_out, not_1_out, h);
  and and_2 (and_2_out, g, not_2_out);
  not not_2 (not_2_out, h);
  or or_4 (Z7, and_1_out, f);
  or or_5 (Z8, and_2_out, f);

  assign BAF = 1'b0;
  assign Z2 = 1'b0;
  assign Z3 = 1'b0;
  assign Z5 = 1'b0;
endmodule
